# Fritzing sketch AR06_RGB (saved by Fritzing 0.9.3b)
breadboards: 1

parts:
  부품1 = Arduino Uno (Rev3)
  Part1 = KY-016 RGB Full Color LED Module [package="Breakout board"]
  LED1 = RGB LED - (4 legs) [package="5 mm [THT]"]  # not connected

nets:
  N1: 부품1.D3_PWM, Part1.R
  N2: 부품1.D5_PWM, Part1.G
  N3: 부품1.D6_PWM, Part1.B
  N4: 부품1.GND, Part1.-

custom parts:
  KY-016 RGB Full Color LED Module: KY-016 Arduino full color 5mm RGB LED, different colors can be obtained by mixing the three primary colors.
